# Fritzing sketch led+shift (saved by Fritzing 0.8.7b)
breadboards: 1

parts:
  Part1 = Arduino Uno (Rev3)
  U1 = SN74LS14N [package="DIP14 [THT]"]
  R1 = Resistor [tolerance=±5% resistance=220 package=THT]
  7_Segment1 = 7 Segment Display
  R2 = Resistor [tolerance=±5% resistance=220 package=THT]
  R3 = Resistor [tolerance=±5% resistance=220 package=THT]
  R4 = Resistor [tolerance=±5% resistance=220 package=THT]
  R5 = Resistor [tolerance=±5% resistance=220 package=THT]
  R6 = Resistor [tolerance=±5% resistance=220 package=THT]
  R7 = Resistor [tolerance=±5% resistance=220 package=THT]
  R8 = Resistor [tolerance=±5% resistance=220 package=THT]

nets:
  GND: Part1.GND, U1.GND, 7_Segment1.common_anode
  N1: Part1.D6_PWM, U1.4Y
  N2: Part1.D7, U1.1A, U1.1Y
  5V: Part1.5V, U1.4A, U1.VCC
  N3: U1.2A, R2.Pin_1
  N4: U1.2Y, R4.Pin_1
  N5: U1.3A, R3.Pin_1
  N6: U1.3Y, R1.Pin_1
  N7: U1.5Y, R5.Pin_1
  N8: U1.5A, R6.Pin_1
  N9: U1.6Y, R7.Pin_1
  N10: U1.6A, R8.Pin_1
  N11: R1.Pin_0, 7_Segment1.Segment_D
  N12: 7_Segment1.Segment_G, R2.Pin_0
  N13: 7_Segment1.Segment_F, R4.Pin_0
  N14: 7_Segment1.Segment_E, R3.Pin_0
  N15: 7_Segment1.Segment_DP, R5.Pin_0
  N16: 7_Segment1.Segment_C, R6.Pin_0
  N17: 7_Segment1.Segment_B, R7.Pin_0
  N18: 7_Segment1.Segment_A, R8.Pin_0
